// Logisim project MIPS32.circ as structural Verilog
module MIPS32 (
);

  wire clock_1_out, de_ex_1_lui_out, de_ex_1_slt_out, de_ex_1_sltu_out, decode_1_lui_out, decode_1_slt_out,
       decode_1_sltu_out;
  wire [3:0] de_ex_1_op_alu_out, decode_1_op_alu_out;
  wire [4:0] de_ex_1_sa_out, decode_1_sa_out;
  wire [31:0] de_ex_1_a_out, de_ex_1_b_out, de_ex_1_ctrl_out, de_ex_1_lui_data_out, decode_1_aout,
       decode_1_b_out, decode_1_ctrl_out, decode_1_lui_data_out, execute_1_c, execute_1_word_out,
       fe_de_1_word_out, fetch_1_word;

  Clock clock_1 (.out(clock_1_out));
  Fetch fetch_1 (.CLK(clock_1_out), .Word(fetch_1_word));
  FE_DE fe_de_1 (.Word_in(fetch_1_word), .CLK(clock_1_out), .Word_out(fe_de_1_word_out));
  Decode decode_1 (
    .Word(fe_de_1_word_out), .Aout(decode_1_aout), .LUI_Data_out(decode_1_lui_data_out),
    .B_out(decode_1_b_out), .Sa_out(decode_1_sa_out), .Ctrl_out(decode_1_ctrl_out),
    .LUI_out(decode_1_lui_out), .Op_ALU_out(decode_1_op_alu_out), .SLT_out(decode_1_slt_out),
    .SLTU_out(decode_1_sltu_out));
  DE_EX de_ex_1 (
    .A_in(decode_1_aout), .LUI_Data_in(decode_1_lui_data_out), .B_in(decode_1_b_out), .CLK(clock_1_out),
    .Sa_in(decode_1_sa_out), .SLT_in(decode_1_slt_out), .SLTU_in(decode_1_sltu_out),
    .LUI_in(decode_1_lui_out), .Ctrl_in(decode_1_ctrl_out), .Op_ALU_in(decode_1_op_alu_out),
    .A_out(de_ex_1_a_out), .LUI_Data_out(de_ex_1_lui_data_out), .B_out(de_ex_1_b_out),
    .Sa_out(de_ex_1_sa_out), .SLT_out(de_ex_1_slt_out), .SLTU_out(de_ex_1_sltu_out),
    .LUI_out(de_ex_1_lui_out), .Ctrl_out(de_ex_1_ctrl_out), .Op_ALU_out(de_ex_1_op_alu_out));
  Execute execute_1 (
    .A(de_ex_1_a_out), .B(de_ex_1_b_out), .LUI_Data(de_ex_1_lui_data_out), .LUI(de_ex_1_lui_out),
    .SLT(de_ex_1_slt_out), .Op_ALU(de_ex_1_op_alu_out), .Sa(de_ex_1_sa_out), .SLTU(de_ex_1_sltu_out),
    .Word_in(de_ex_1_ctrl_out), .C(execute_1_c), .Word_out(execute_1_word_out));
  EX_ME ex_me_1 (.Word_in(execute_1_word_out), .CLK(clock_1_out), .C_in(execute_1_c));  // open: Word_out, C_out
endmodule

module Fetch (
  input  CLK,
  output [31:0] Word
);

  wire [1:0] incrementer_1_p3;
  wire [29:0] incrementer_1_p1, incrementer_1_p2;

  // Incrementer #(.width(30)) incrementer_1: pin names not known; wires that end beside it: incrementer_1_p1, incrementer_1_p2, {incrementer_1_p1, incrementer_1_p3}
  Register #(.width(32)) register_1 (
    .D({incrementer_1_p2, incrementer_1_p3}), .en(CLK), .clk(CLK), .Q({incrementer_1_p1, incrementer_1_p3}));  // open: clr
  // MIPSProgramROM mipsprogramrom_1: pin names not known; wires that end beside it: Word

  // Notes on the sheet:
  //   contents of mipsprogramrom_1 (hex, n*v repeats v):
  //   ADDIU $t2, $zero, 1 ADDU $v0, $t1, $t2 ADDU $t1, $zero, $t2 ADDU $t2, $zero, $v0 ADDU $v0, $t1, $t2
  //   ADDU $t1, $zero, $t2 ADDU $t2, $zero, $v0 ADDU $v0, $t1, $t2 ADDU $t1, $zero, $t2 ADDU $t2, $zero,
  //   $v0
endmodule

module Decode (
  input  [31:0] Word,
  output [31:0] Aout,
  output [31:0] LUI_Data_out,
  output [31:0] B_out,
  output [4:0] Sa_out,
  output [31:0] Ctrl_out,
  output LUI_out,
  output [3:0] Op_ALU_out,
  output SLT_out,
  output SLTU_out
);

  wire [4:0] multiplexer_1_out, multiplexer_2_out;
  wire [31:0] bit_extender_2_out, bit_extender_3_out, multiplexer_4_out, registerfile_1_p5;

  assign LUI_Data_out[15:0] = {{15{Word[30]}}, Word[30]};  // Bit_Extender bit_extender_1
  Multiplexer #(.width(5), .enable("false")) multiplexer_1 (
    .in0(Word[15:11]), .in1(Word[20:16]), .out(multiplexer_1_out), .sel(Word[29]));
  assign bit_extender_2_out = {{16{Word[15]}}, Word[15:0]};  // Bit_Extender bit_extender_2
  assign bit_extender_3_out = {{16{1'b0}}, Word[15:0]};  // Bit_Extender bit_extender_3
  Multiplexer #(.width(5), .enable("false")) multiplexer_2 (
    .in0(multiplexer_1_out), .in1(Word[20:16]), .out(multiplexer_2_out), .sel(Word[31]));
  Controls controls_1 (
    .Opcode(Word[31:26]), .Funct(Word[5:0]), .LUI(LUI_out), .Op_ALU(Op_ALU_out), .SLT(SLT_out),
    .SLTU(SLTU_out));
  // RegisterFile registerfile_1: pin names not known; wires that end beside it: multiplexer_2_out, Word[25:21], Word[20:16], Aout, registerfile_1_p5
  Multiplexer #(.width(32), .enable("false")) multiplexer_3 (
    .in0(registerfile_1_p5), .in1(multiplexer_4_out), .out(B_out), .sel(Word[29]));
  Multiplexer #(.width(32), .enable("false")) multiplexer_4 (
    .in0(bit_extender_2_out), .in1(bit_extender_3_out), .out(multiplexer_4_out), .sel(Word[28]));

  assign Ctrl_out = Word;
  assign LUI_Data_out[31:16] = Word[15:0];
  assign Sa_out = Word[10:6];
endmodule

module Controls (
  input  [5:0] Opcode,
  input  [5:0] Funct,
  output LUI,
  output [3:0] Op_ALU,
  output SLT,
  output SLTU
);

  wire and_1_out, and_2_out, and_4_out, and_5_out, and_6_out, not_1_out, not_4_out;
  wire [3:0] multiplexer_1_out;
  wire [3:1] not_2_out;

  and and_1 (and_1_out, Funct[3], Funct[0], Funct[1]);
  not not_1 (not_1_out, Funct[2]);
  and and_2 (and_2_out, not_1_out, Funct[3]);
  not not_2 (not_2_out[1], Funct[4]);
  not not_3 (not_2_out[3], Funct[4]);
  and and_3 (LUI, Opcode[0], Opcode[1], Opcode[2]);
  not not_4 (not_4_out, Opcode[2]);
  and and_4 (and_4_out, Opcode[1], not_4_out);
  Multiplexer #(.width(4), .enable("false")) multiplexer_1 (
    .in0({Funct[2:0], Funct[5]}), .in1({not_2_out[3], Funct[4], not_2_out[1], Funct[4]}),
    .out(multiplexer_1_out), .sel(and_1_out));
  Multiplexer #(.width(4), .enable("false")) multiplexer_2 (
    .in0({Opcode[2:0], Opcode[5]}), .in1(multiplexer_1_out), .out(Op_ALU), .sel(Opcode[3]));
  or or_1 (SLT, and_4_out, and_2_out);
  and and_5 (and_5_out, and_4_out, Opcode[0]);
  and and_6 (and_6_out, Funct[0], and_2_out);
  or or_2 (SLTU, and_5_out, and_6_out);

  // Notes on the sheet:
  //   Arith
endmodule

module Execute (
  input  [31:0] A,
  input  [31:0] B,
  input  [31:0] LUI_Data,
  input  LUI,
  input  SLT,
  input  [3:0] Op_ALU,
  input  [4:0] Sa,
  input  SLTU,
  input  [31:0] Word_in,
  output [31:0] C,
  output [31:0] Word_out
);

  wire and_1_out, and_2_out, comparator_1_eq, comparator_1_lt, comparator_2_eq, comparator_2_lt,
       multiplexer_2_out, not_1_out, not_2_out;
  wire [31:0] bit_extender_1_out, mips_alu_1_p5, multiplexer_1_out;

  // Mips_ALU mips_alu_1: pin names not known; wires that end beside it: A, B, Op_ALU, Sa, mips_alu_1_p5
  Comparator #(.width(32)) comparator_1 (.a(A), .b(B), .eq(comparator_1_eq), .lt(comparator_1_lt));  // open: gt
  Comparator #(.width(32), .mode("unsigned")) comparator_2 (
    .a(A), .b(B), .eq(comparator_2_eq), .lt(comparator_2_lt));  // open: gt
  not not_1 (not_1_out, comparator_1_eq);
  not not_2 (not_2_out, comparator_2_eq);
  Multiplexer #(.width(32), .enable("false")) multiplexer_1 (
    .in0(mips_alu_1_p5), .in1(LUI_Data), .out(multiplexer_1_out), .sel(LUI));
  and and_1 (and_1_out, not_1_out, comparator_1_lt);
  and and_2 (and_2_out, not_2_out, comparator_2_lt);
  Multiplexer #(.enable("false")) multiplexer_2 (.in0(and_1_out), .in1(and_2_out), .out(multiplexer_2_out), .sel(SLTU));
  Multiplexer #(.width(32), .enable("false")) multiplexer_3 (
    .in0(multiplexer_1_out), .in1(bit_extender_1_out), .out(C), .sel(SLT));
  assign bit_extender_1_out = {{31{1'b0}}, multiplexer_2_out};  // Bit_Extender bit_extender_1

  assign Word_out = Word_in;

  // Notes on the sheet:
  //   SLT
  //   SLTU
endmodule

module Memory (
);

  // LCD_Video lcd_video_1: pin names not known
endmodule

module DE_EX (
  input  [31:0] A_in,
  input  [31:0] LUI_Data_in,
  input  [31:0] B_in,
  input  CLK,
  input  [4:0] Sa_in,
  input  SLT_in,
  input  SLTU_in,
  input  LUI_in,
  input  [31:0] Ctrl_in,
  input  [3:0] Op_ALU_in,
  output [31:0] A_out,
  output [31:0] LUI_Data_out,
  output [31:0] B_out,
  output [4:0] Sa_out,
  output SLT_out,
  output SLTU_out,
  output LUI_out,
  output [31:0] Ctrl_out,
  output [3:0] Op_ALU_out
);

  Register #(.width(32)) A_reg (.D(A_in), .en(CLK), .clk(CLK), .Q(A_out));  // open: clr
  Register #(.width(32)) LUI_Data_reg (.D(LUI_Data_in), .en(CLK), .clk(CLK), .Q(LUI_Data_out));  // open: clr
  Register #(.width(32)) B_reg (.D(B_in), .en(CLK), .clk(CLK), .Q(B_out));  // open: clr
  Register #(.width(5)) Sa_reg (.D(Sa_in), .en(CLK), .clk(CLK), .Q(Sa_out));  // open: clr
  Register #(.width(1)) SLTU_reg (.D(SLTU_in), .en(CLK), .clk(CLK), .Q(SLTU_out));  // open: clr
  Register #(.width(1)) LUI_reg (.D(LUI_in), .en(CLK), .clk(CLK), .Q(LUI_out));  // open: clr
  Register #(.width(32)) Ctrl_reg (.D(Ctrl_in), .en(CLK), .clk(CLK), .Q(Ctrl_out));  // open: clr
  Register #(.width(4)) Op_ALU_reg (.D(Op_ALU_in), .en(CLK), .clk(CLK), .Q(Op_ALU_out));  // open: clr
  Register #(.width(1)) SLT_reg (.D(SLT_in), .en(CLK), .clk(CLK), .Q(SLT_out));  // open: clr
endmodule

module FE_DE (
  input  [31:0] Word_in,
  input  CLK,
  output [31:0] Word_out
);

  Register #(.width(32)) register_1 (.D(Word_in), .en(CLK), .clk(CLK), .Q(Word_out));  // open: clr
endmodule

module EX_ME (
  input  [31:0] Word_in,
  input  CLK,
  input  [31:0] C_in,
  output [31:0] Word_out,
  output [31:0] C_out
);

  Register #(.width(32)) register_1 (.D(Word_in), .en(CLK), .clk(CLK), .Q(Word_out));  // open: clr
  Register #(.width(32)) register_2 (.D(C_in), .en(CLK), .clk(CLK), .Q(C_out));  // open: clr
endmodule
